// Digital circuit cpu.dig as structural Verilog
module cpu (
  input  clk
);

  wire clear_2_out, clear_3_out, clear_4_out, clear_out, share_out;
  wire [3:0] load_2_out, load_3_out, load_4_out, load_out;
  wire [15:0] driver_1_out, register_16bits_1_out;

  DipSwitch share (.out(share_out));
  DipSwitch load (.out(load_out[0]));
  DipSwitch enabled (.out(load_out[1]));
  DipSwitch count (.out(load_out[2]));
  DipSwitch direction (.out(load_out[3]));
  DipSwitch clear (.out(clear_out));
  DipSwitch load_2 (.out(load_2_out[0]));
  DipSwitch enabled_2 (.out(load_2_out[1]));
  DipSwitch count_2 (.out(load_2_out[2]));
  DipSwitch direction_2 (.out(load_2_out[3]));
  DipSwitch clear_2 (.out(clear_2_out));
  DipSwitch load_3 (.out(load_3_out[0]));
  DipSwitch enabled_3 (.out(load_3_out[1]));
  DipSwitch count_3 (.out(load_3_out[2]));
  DipSwitch direction_3 (.out(load_3_out[3]));
  DipSwitch clear_3 (.out(clear_3_out));
  DipSwitch load_4 (.out(load_4_out[0]));
  DipSwitch enabled_4 (.out(load_4_out[1]));
  DipSwitch count_4 (.out(load_4_out[2]));
  DipSwitch direction_4 (.out(load_4_out[3]));
  DipSwitch clear_4 (.out(clear_4_out));
  LED led_1 (.in(register_16bits_1_out[15]));
  LED led_2 (.in(register_16bits_1_out[14]));
  register_16bits register_16bits_1 (
    .in(driver_1_out), .clk(clk), .ctrl(load_out), .clr(clear_out), .out(register_16bits_1_out));  // open: ival, ovf
  register_16bits register_16bits_2 (
    .in(driver_1_out), .clk(clk), .ctrl(load_2_out), .clr(clear_2_out), .out(register_16bits_1_out));  // open: ival, ovf
  register_16bits register_16bits_3 (
    .in(driver_1_out), .clk(clk), .ctrl(load_3_out), .clr(clear_3_out), .out(register_16bits_1_out));  // open: ival, ovf
  register_16bits register_16bits_4 (
    .in(driver_1_out), .clk(clk), .ctrl(load_4_out), .clr(clear_4_out), .out(register_16bits_1_out));  // open: ival, ovf
  LED led_3 (.in(register_16bits_1_out[13]));
  LED led_4 (.in(register_16bits_1_out[12]));
  LED led_5 (.in(register_16bits_1_out[11]));
  LED led_6 (.in(register_16bits_1_out[10]));
  LED led_7 (.in(register_16bits_1_out[9]));
  LED led_8 (.in(register_16bits_1_out[8]));
  LED led_9 (.in(register_16bits_1_out[7]));
  LED led_10 (.in(register_16bits_1_out[6]));
  assign driver_1_out = share_out ? register_16bits_1_out : 16'bz;  // Driver driver_1
  LED led_11 (.in(register_16bits_1_out[5]));
  LED led_12 (.in(register_16bits_1_out[4]));
  LED led_13 (.in(register_16bits_1_out[3]));
  LED led_14 (.in(register_16bits_1_out[2]));
  DipSwitch d15 (.out(driver_1_out[0]));
  DipSwitch d14 (.out(driver_1_out[1]));
  DipSwitch d13 (.out(driver_1_out[2]));
  DipSwitch d12 (.out(driver_1_out[3]));
  DipSwitch d11 (.out(driver_1_out[4]));
  DipSwitch d10 (.out(driver_1_out[5]));
  DipSwitch d9 (.out(driver_1_out[6]));
  DipSwitch d8 (.out(driver_1_out[7]));
  DipSwitch d7 (.out(driver_1_out[8]));
  DipSwitch d6 (.out(driver_1_out[9]));
  DipSwitch d5 (.out(driver_1_out[10]));
  DipSwitch d4 (.out(driver_1_out[11]));
  DipSwitch d3 (.out(driver_1_out[12]));
  DipSwitch d2 (.out(driver_1_out[13]));
  DipSwitch d1 (.out(driver_1_out[14]));
  DipSwitch d0 (.out(driver_1_out[15]));
  LED led_15 (.in(register_16bits_1_out[1]));
  LED led_16 (.in(register_16bits_1_out[0]));

  // Notes on the sheet:
  //   clk: Hz: 5
endmodule
