// Digital circuit register-16bits.dig as structural Verilog
module register_16bits (
  input  [15:0] in,
  input  clk,
  input  [3:0] ctrl,
  input  clr,
  output [15:0] out,
  output [15:0] ival,
  output [15:0] ovf
);

  CounterPreset #(.Bits(16)) counterpreset_1 (
    .en(ctrl[2]), .C(clk), .dir(ctrl[3]), .in(in), .ld(ctrl[0]), .clr(clr), .out(ival), .ovf(ovf[0]));
  assign out = ctrl[1] ? ival : 16'bz;  // Driver driver_1
  // Pins of 1 and 16 bits meet at ovf

  // Notes on the sheet:
  //   in: Data input
  //   clk: Clock
  //   ctrl: Register control:
  //   bit 0 - load, 
  //   bit 1 - out enabled, 
  //   bit 2 - counter enabled, 
  //   bit 3 - counter direction (0 - up | 1 - down)
  //   clr: Clear register
  //   out: Register out
  //   ival: Register internal value
  //   ovf: Register overflow
endmodule
