// Digital circuit test.dig as structural Verilog
module test (
  input  clk
);

  wire Clear_out, counterpreset_1_out, counterpreset_1_ovf, counterpreset_2_out, counterpreset_2_ovf,
       counterpreset_3_out, counterpreset_3_ovf, Dir_out, Enable_out, Load_out, undriven, undriven_2;

  DipSwitch Dir (.out(Dir_out));
  DipSwitch Clear (.out(Clear_out));
  DipSwitch Load (.out(Load_out));
  DipSwitch Enable (.out(Enable_out));
  LED led_1 (.in(counterpreset_1_ovf));
  CounterPreset counterpreset_1 (
    .en(Enable_out), .C(clk), .dir(Dir_out), .in(undriven), .ld(Load_out), .clr(Clear_out),
    .out(counterpreset_1_out), .ovf(counterpreset_1_ovf));
  LED led_2 (.in(counterpreset_1_out));
  CounterPreset counterpreset_2 (
    .en(Enable_out), .C(clk), .dir(Dir_out), .in(undriven_2), .ld(Load_out), .clr(Clear_out),
    .out(counterpreset_2_out), .ovf(counterpreset_2_ovf));
  LED led_3 (.in(counterpreset_2_out));
  CounterPreset counterpreset_3 (
    .en(Enable_out), .C(clk), .dir(Dir_out), .in(1'b0), .ld(Load_out), .clr(Clear_out),
    .out(counterpreset_3_out), .ovf(counterpreset_3_ovf));
  LED led_4 (.in(counterpreset_3_out));
endmodule
